# Fritzing sketch PICAXE-08M2-blink (saved by Fritzing 0.9.0b)
breadboards: 1
perfboards: 1

parts:
  LED1 = smd LED [color="Green (570nm)" package="0603 [SMD]"]
  R1 = Resistor [tolerance=±20% resistance=330 package=THT]  # not connected
  R2 = Resistor [tolerance=±5% resistance=10k package=THT]  # not connected
  R3 = Resistor [tolerance=±5% resistance=22k package=THT]  # not connected
  TRS1 = Audio Jack (TRS) 3.5mm [package="4Ucon 08780 [THT]"]  # not connected
  VCC1 = Battery
  IC1 = PICAXE-08M [part_number=PICAXE-08m2 package=THT]  # not connected

nets:
  N1: LED1.cathode, VCC1.+

notes:
  O1
  IN
  O2
  0V
  18=O1
  28=O2
